// Logisim project ukladyzmultiplekserem.circ as structural Verilog: 1 circuit, main circuit main
module main (
  input  True,
  input  False,
  input  a,
  input  b,
  input  c,
  input  d,
  input  [3:0] a_b_c_d,
  input  in_8,
  input  True_2,
  input  False_2,
  input  a_2,
  input  b_2,
  input  [2:0] a_b_c,
  input  in_14,
  input  c_2
);

  wire multiplexer_1_out, multiplexer_2_out, nand_1_out, nand_2_out, nand_3_out, nand_4_out, nand_5_out,
       not_1_out, not_2_out, not_3_out, not_4_out, not_5_out, not_6_out, not_7_out, not_8_out, not_9_out,
       not_10_out, not_11_out, not_12_out, or_1_out, or_2_out;

  not not_1 (not_1_out, a);
  not not_2 (not_2_out, b);
  not not_3 (not_3_out, c);
  not not_4 (not_4_out, d);
  not not_5 (not_5_out, c_2);
  not not_6 (not_6_out, a_2);
  not not_7 (not_7_out, b_2);
  nand nand_1 (nand_1_out, not_1_out, not_2_out, not_4_out);
  not not_8 (not_8_out, nand_1_out);
  not not_9 (not_9_out, nand_2_out);
  nand nand_2 (nand_2_out, not_3_out, not_4_out);
  nand nand_3 (nand_3_out, not_5_out, not_6_out);
  not not_10 (not_10_out, nand_3_out);
  nand nand_4 (nand_4_out, a_2, not_7_out);
  not not_11 (not_11_out, nand_4_out);
  not not_12 (not_12_out, nand_5_out);
  nand nand_5 (nand_5_out, b_2, c_2);
  or or_1 (or_1_out, not_8_out, not_9_out);
  LED led_1 (.in(or_1_out));
  or or_2 (or_2_out, not_10_out, not_11_out, not_12_out);
  LED led_2 (.in(or_2_out));
  Multiplexer #(.select(4)) multiplexer_1 (
    .in0(True), .in1(True), .in2(True), .in3(True), .in4(False), .in5(False), .in6(False), .in7(False),
    .in8(True), .in9(False), .in10(False), .in11(False), .in12(False), .in13(False), .in14(False),
    .in15(False), .out(multiplexer_1_out), .sel(a_b_c_d), .en(in_8));
  LED led_3 (.in(multiplexer_1_out));
  Multiplexer #(.select(3)) multiplexer_2 (
    .in0(True_2), .in1(False_2), .in2(True_2), .in3(True_2), .in4(True_2), .in5(True_2), .in6(False_2),
    .in7(True_2), .out(multiplexer_2_out), .sel(a_b_c), .en(in_14));
  LED led_4 (.in(multiplexer_2_out));

  // Notes on the sheet:
  //   przykład 1.
  //   przykład 2
  //   00
  //   AB
  //   CD
  //   00
  //   1
  //   01
  //   0
  //   11
  //   0
  //   1
  //   10
  //   AB
  //   C
  //   0
  //   1
  //   01
  //   11
  //   10
  //   1
  //   1
  //   1
  //   0
  //   0
  //   0
  //   0
  //   0
  //   0
  //   0
  //   0
  //   0
  //   01
  //   00
  //   11
  //   10
  //   1
  //   1
  //   1
  //   0
  //   1
  //   1
  //   1
  //   0
endmodule
