// Logisim project lab4.circ as structural Verilog: 1 circuit, main circuit main
module main (
  input  Bramka_NOT,
  input  Bramka_AND,
  input  in_3
);

  wire button_1_out, clock_1_out, transistor_1_out, transistor_2_out, transistor_3_out;
  wire [7:0] counter_1_q, counter_2_q;

  Button button_1 (.out(button_1_out));
  Clock clock_1 (.out(clock_1_out));
  Transistor transistor_1 (.in(1'b1), .out(transistor_1_out), .gate(Bramka_NOT));
  LED led_1 (.in(transistor_1_out));
  Transistor transistor_2 (.in(1'b0), .out(transistor_2_out), .gate(Bramka_AND));
  Transistor transistor_3 (.in(transistor_2_out), .out(transistor_3_out), .gate(in_3));
  Counter counter_1 (.Q(counter_1_q), .clk(button_1_out));  // open: load, D, count, carry, clr
  Counter counter_2 (.Q(counter_2_q), .clk(clock_1_out));  // open: load, D, count, carry, clr
  Transistor #(.\type ("n"), .gate("br")) transistor_4 (.in(Bramka_AND), .out(transistor_3_out), .gate(in_3));
  LED led_2 (.in(transistor_3_out));
  Transistor #(.\type ("n")) transistor_5 (.in(in_3), .out(transistor_3_out), .gate(Bramka_AND));
  Hex_Digit_Display hex_digit_display_1 (.value(counter_1_q[3:0]));  // open: dp
  Hex_Digit_Display hex_digit_display_2 (.value(counter_1_q[7:4]));  // open: dp
  Hex_Digit_Display hex_digit_display_3 (.value(counter_2_q[3:0]));  // open: dp
  Hex_Digit_Display hex_digit_display_4 (.value(counter_2_q[7:4]));  // open: dp

  // Notes on the sheet:
  //   Licznik kliknięć
  //   Zegar do gotowania jajek
endmodule
